// Logisim project latches.circ as structural Verilog: 1 circuit, main circuit main
module main (
  input  R,
  input  S,
  input  S_2,
  input  R_2,
  output Q,
  output Q_2
);

  wire nand_1_out, nor_1_out, not_1_out, not_2_out;

  not not_1 (not_1_out, S_2);
  not not_2 (not_2_out, R_2);
  nor nor_1 (nor_1_out, S, Q);
  nand nand_1 (nand_1_out, not_2_out, Q_2);
  nor nor_2 (Q, R, nor_1_out);
  LED led_1 (.in(Q));
  nand nand_2 (Q_2, not_1_out, nand_1_out);
  LED led_2 (.in(Q_2));

  // Notes on the sheet:
  //   RS-NOR-latch with reset priority
  //   SR-NAND-latch with set priority
endmodule
